# Fritzing sketch circuitschematiz (saved by Fritzing 1.0.0rc)
circuit board: 8.46667cm x 5.64444cm
breadboards: 1

parts:
  Arduino_PRO_MINI = Arduino Pro Mini (5V)
  IR1 = TSOP312.., 314.. [package=THT]
  Part2 = FTDI Basic Programmer
  CONN1 = USB connector [package=THT]
  K10 = Relay [part_number=FRS1B-S package=THT]
  K11 = Relay [part_number=FRS1B-S package=THT]
  K12 = Relay [part_number=FRS1B-S package=THT]
  K13 = Relay [part_number=FRS1B-S package=THT]
  U7 = Sharp PC817 [package=THT]
  U8 = Sharp PC817 [package=THT]
  U9 = Sharp PC817 [package=THT]
  U10 = Sharp PC817 [package=THT]
  Q6 = NPN-Transistor [package="TO92 [THT]"]
  Q7 = NPN-Transistor [package="TO92 [THT]"]
  Q8 = NPN-Transistor [package="TO92 [THT]"]
  Q9 = NPN-Transistor [package="TO92 [THT]"]
  D6 = Rectifier Diode [part_number=1N4001 package="300 mil [THT]"]
  D7 = Rectifier Diode [part_number=1N4001 package="300 mil [THT]"]
  D8 = Rectifier Diode [part_number=1N4001 package="300 mil [THT]"]
  D9 = Rectifier Diode [part_number=1N4001 package="300 mil [THT]"]
  J16 = male pin header, 2 pins [form="♂ (male)"]
  R11 = Resistor [tolerance=±5% power=0.25W resistance=220 package=THT]
  R12 = Resistor [tolerance=±5% power=0.25W resistance=220 package=THT]
  R13 = Resistor [tolerance=±5% power=0.25W resistance=220 package=THT]
  R14 = Resistor [tolerance=±5% power=0.25W resistance=220 package=THT]
  R15 = Resistor [tolerance=±5% power=0.25W resistance=220 package=THT]
  R16 = Resistor [tolerance=±5% power=0.25W resistance=220 package=THT]
  R17 = Resistor [tolerance=±5% power=0.25W resistance=220 package=THT]
  R18 = Resistor [tolerance=±5% power=0.25W resistance=220 package=THT]
  J17 = Camdenboss CTB0158-3 [part_number=CTB0158-3 package=THT]
  J18 = Camdenboss CTB0158-3 [part_number=CTB0158-3 package=THT]
  J19 = Camdenboss CTB0158-3 [part_number=CTB0158-3 package=THT]
  J20 = Camdenboss CTB0158-3 [part_number=CTB0158-3 package=THT]
  J21 = Camdenboss CTB0158-6 [part_number=CTB0158-6 package=THT]
  V1 = AC Power [voltage=240 frequency=60]
  LED1 = LED - 5mm [color="Yellow (592nm)" current=0.030A package="5 mm [THT]"]
  LED2 = LED - 5mm [color="Red (633nm)" current=0.030A package="5 mm [THT]"]
  LED3 = LED - 5mm [color="Green (555nm)" current=0.030A package="5 mm [THT]"]
  V2 = DC Power [voltage=5]

nets:
  N1: Arduino_PRO_MINI.DTR, Part2.DTR
  VCC: Arduino_PRO_MINI.VCC, IR1.Vs, Part2.POWER, CONN1.5V, J21.terminal_1, V2.V+
  GND: Arduino_PRO_MINI.GND, IR1.Data, Part2.CTS, Part2.GND, CONN1.GND, Q6.E, Q7.E, Q8.E, Q9.E, J21.pin6, J21.terminal_6, V2.V-
  N2: Arduino_PRO_MINI.D6, J21.terminal_5
  N3: Arduino_PRO_MINI.D5, J21.terminal_4
  N4: Arduino_PRO_MINI.D4, J21.terminal_3
  N5: Arduino_PRO_MINI.D3, J21.terminal_2
  N6: Arduino_PRO_MINI.D2, IR1.GND
  N7: Arduino_PRO_MINI.RXI, Part2.TXO
  N8: Arduino_PRO_MINI.TXO, Part2.RXI
  N9: K10.A, J20.pin3
  N10: K10.COIL1, Q9.C, D6.anode
  N11: K10.C1, K10.C2, J20.pin2
  N12: K10.COIL2, K11.COIL2, K12.COIL2, K13.COIL2, U7.Pin_4, U8.Pin_4, U9.Pin_4, U10.Pin_4, D6.cathode, D7.cathode, D8.cathode, D9.cathode, J16.pin1, J16.pin2, R13.Pin_0, R14.Pin_0, R16.Pin_0, R18.Pin_0, J21.pin1
  N13: K10.B, J20.pin1
  N14: K11.A, J19.pin3
  N15: K11.COIL1, Q7.C, D9.anode
  N16: K11.C1, K11.C2, J19.pin2
  N17: K11.B, J19.pin1
  N18: K12.A, J17.pin3
  N19: K12.COIL1, Q8.C, D8.anode
  N20: K12.C1, K12.C2, J17.pin2
  N21: K12.B, J17.pin1
  N22: K13.A, J18.pin3
  N23: K13.COIL1, Q6.C, D7.anode
  N24: K13.C1, K13.C2, J18.pin2
  N25: K13.B, J18.pin1
  N26: U7.Pin_1, R16.Pin_1
  N27: U7.Pin_2, J21.pin2
  N28: U7.Pin_3, R17.Pin_0
  N29: U8.Pin_1, R18.Pin_1
  N30: U8.Pin_2, J21.pin4
  N31: U8.Pin_3, R11.Pin_0
  N32: U9.Pin_1, R13.Pin_1
  N33: U9.Pin_2, J21.pin3
  N34: U9.Pin_3, R15.Pin_0
  N35: U10.Pin_1, R14.Pin_1
  N36: U10.Pin_2, J21.pin5
  N37: U10.Pin_3, R12.Pin_0
  N38: Q6.B, R12.Pin_1
  N39: Q7.B, R17.Pin_1
  N40: Q8.B, R11.Pin_1
  N41: Q9.B, R15.Pin_1
  N42: J17.terminal_2, J19.terminal_2, J20.terminal_2
  N43: J17.terminal_3, LED3.anode
  N44: J19.terminal_3, LED2.anode
  N45: J20.terminal_3, LED1.anode
  live: V1.V+
  neutral: V1.V-, LED1.cathode, LED2.cathode, LED3.cathode

notes:
  usb
  AUS Traffic Light sequencer schematic, 1.666
  When programming the ftdi programmer will be used, once programmed the ftdi adapter gets removed and use 5v usb power
  4 channel relay module
  this relay is unused and is spare

custom parts:
  TSOP312.., 314..: The TSOP312.., TSOP314.. series are miniaturized receivers for infrared remote control systems. A PIN diode and a preamplifier are assembled on a lead frame, the epoxy package acts as an IR filter. The demodulated output signal can be directly decoded by a microprocessor. The TSOP312.. is compatible with all common IR remote control data formats. The TSOP314.. is optimized to suppress almost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
